# Fritzing sketch voltage divider 3_28_25 (saved by Fritzing 1.0.4)
breadboards: 1

parts:
  U1 = Voltage Regulator - 5V [package="TO220 [THT]"]
  C1 = Capacitor Polarized [package=panasonic_c]
  C2 = Capacitor Polarized [package=panasonic_c]
  R2 = Basic Force Sensing Resistor (FSR) [package=THT]
  R1 = Resistor [tolerance=±5% power=0.25W resistance=220 package=THT]
  Adafruit_MCP3421_18-Bit_ADC1 = Adafruit MCP3421 18-Bit ADC [part_number=#5870]
  U2 = OP27 - Low Noise, Precision Op Amp [part_number=OP27]
  R3 = Resistor [tolerance=±5% power=0.25W resistance=220 package=THT]
  C3 = Ceramic Capacitor [capacitance="100 nF" voltage=35V package="0603 [SMD, multilayer]"]
  Part1 = Adafruit LM4040 Voltage Reference [part_number="Adafruit #2200"]
  C4 = Ceramic Capacitor [capacitance="100 nF" voltage=35V package="0603 [SMD, multilayer]"]

nets:
  N1: U1.input_voltage, C1.-
  GND: U1.GND, C1.+, C2.-, U2.-V, C3.0, Part1.GND, C4.1
  N2: U1.output_voltage, C2.+, R1.Pin_0, U2.TRIM#8, Part1.VIN
  N3: R2.pin_1, R1.Pin_1, U2.+IN, C4.0
  N4: R2.pin_2, U2.-IN
  N5: Adafruit_MCP3421_18-Bit_ADC1.VIN+, R3.Pin_0, C3.1
  N6: Adafruit_MCP3421_18-Bit_ADC1.VIN-, Part1.2.048V
  N7: U2.TRIM#1, R3.Pin_1

custom parts:
  Adafruit MCP3421 18-Bit ADC: The Adafruit MCP3421 18-Bit ADC is a simple, inexpensive, and easy to use 18-bit, 240 SPS, single-channel ADC with an I2C interface that can run up to 3.4MHz clock rate. A perfect component whenever you need an ADC that has differential inputs, adjustable gain, and a built in precision/low-drift reference voltage. One of the trade-offs with getting 18-bit precision is that the ADC is not going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
  Adafruit LM4040 Voltage Reference: How good is your multimeter really? Or maybe your analog converter needs a good reference? Or lets say you want to test your microcontroller's conversion accuracy & precision. If only you had a dependable, high precision, rock-solid voltage reference. Now you know why we made this very cute and useful little breakout board. It has two very high precision shunt-type voltage references with 750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
