# Fritzing sketch bender PCB for presentation (saved by Fritzing 1.0.3b)

parts:
  Adafruit_MCP3421_18-Bit_ADC1 = Adafruit MCP3421 18-Bit ADC [part_number=#5870]
  Adafruit_Qwiic_/_Stemma_QT_5_Port_Hub1 = Adafruit Qwiic / Stemma QT 5 Port Hub [part_number=#5625]
  Adafrit_Precision_Volt_Ref = Adafruit LM4040 Voltage Reference [part_number="Adafruit #2200"]
  100_ohm = Resistor [tolerance=±5% power=0.25W resistance=220 package=THT]
  Part1 = Arduino Uno (Rev3) - ICSP
  J1 = Basic Force Sensing Resistor (FSR) [package=THT]
  Part2 = Adafruit BNO055 STEMMA QT [part_number="Adafruit #4646"]
  RE1 = Rotary Encoder [package=THT]

nets:
  VCC: Adafruit_MCP3421_18-Bit_ADC1.VCC, Adafruit_Qwiic_/_Stemma_QT_5_Port_Hub1.VCC
  GND: Adafruit_MCP3421_18-Bit_ADC1.GND, Adafruit_Qwiic_/_Stemma_QT_5_Port_Hub1.GND
  N1: Adafruit_MCP3421_18-Bit_ADC1.SCL, Adafruit_Qwiic_/_Stemma_QT_5_Port_Hub1.SCL, Part1.A4/SDA, Part2.SCL
  N2: Adafruit_MCP3421_18-Bit_ADC1.SDA, Adafruit_Qwiic_/_Stemma_QT_5_Port_Hub1.SDA, Part1.A5/SCL, Part2.SDA
  N3: Adafruit_MCP3421_18-Bit_ADC1.VIN+, Part1.GND, J1.pin_0
  N4: Adafruit_MCP3421_18-Bit_ADC1.VIN-, 100_ohm.Pin_1, J1.pin_1
  VIN: Adafrit_Precision_Volt_Ref.VIN, Part1.5V
  N5: Adafrit_Precision_Volt_Ref.4.096V, 100_ohm.Pin_0
  N6: Part1.A0, RE1.EncoderPinA

custom parts:
  Adafruit MCP3421 18-Bit ADC: The Adafruit MCP3421 18-Bit ADC is a simple, inexpensive, and easy to use 18-bit, 240 SPS, single-channel ADC with an I2C interface that can run up to 3.4MHz clock rate. A perfect component whenever you need an ADC that has differential inputs, adjustable gain, and a built in precision/low-drift reference voltage. One of the trade-offs with getting 18-bit precision is that the ADC is not going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
  Adafruit Qwiic / Stemma QT 5 Port Hub: Qwiic, or STEMMA QT, is a very efficient way to quickly prototype an idea, but a lot of Qwiic/Stemma QT driver boards only have one port, and devices have two ports but that's only good for chaining. Maybe you want to reduce your I2C line capacitance by having a star formation instead of a looooong chain. Or maybe its just easier for your mechanical layout to have them closer to a central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
  Adafruit LM4040 Voltage Reference: How good is your multimeter really? Or maybe your analog converter needs a good reference? Or lets say you want to test your microcontroller's conversion accuracy & precision. If only you had a dependable, high precision, rock-solid voltage reference. Now you know why we made this very cute and useful little breakout board. It has two very high precision shunt-type voltage references with 750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
  Adafruit BNO055 STEMMA QT: If you've ever ordered and wire up a 9-DOF sensor, chances are you've also realized the challenge of turning the sensor data from an accelerometer, gyroscope, and magnetometer into actual "3D space orientation"! Orientation is a hard problem to solve. The sensor fusion algorithms (the secret sauce that blends accelerometer, magnetometer, and gyroscope data into stable three-axis orientation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
