# Fritzing sketch bender PCB (saved by Fritzing 1.0.3b)
circuit board: 12.405cm x 7.73298cm

parts:
  Adafruit_MCP3421_18-Bit_ADC1 = Adafruit MCP3421 18-Bit ADC [part_number=#5870]
  Adafruit_Qwiic_/_Stemma_QT_5_Port_Hub1 = Adafruit Qwiic / Stemma QT 5 Port Hub [part_number=#5625]
  Adafrit_Precision_Volt_Ref = Adafruit LM4040 Voltage Reference [part_number="Adafruit #2200"]
  100_ohm = Resistor [tolerance=±5% power=0.25W resistance=220 package=THT]
  Strain_Sensor_Vmeasure = Camdenboss CTB0158-2 [part_number=CTB0158-2 package=THT]
  5V = female pin header, 6 pins [form="♀ (female)"]
  Arduino_Nano = Arduino Nano (Rev3.0)
  D9_/_A0 = female pin header, 2 pins [form="♀ (female)"]
  GND = female pin header, 6 pins [form="♀ (female)"]

nets:
  GND: Adafruit_MCP3421_18-Bit_ADC1.VIN+, Adafruit_Qwiic_/_Stemma_QT_5_Port_Hub1.GND, Adafrit_Precision_Volt_Ref.GND, Strain_Sensor_Vmeasure.pin2, Arduino_Nano.GND, GND.pin1, GND.pin2, GND.pin3, GND.pin4, GND.pin5, GND.pin6
  N1: Adafruit_MCP3421_18-Bit_ADC1.VIN-, 100_ohm.Pin_1, Strain_Sensor_Vmeasure.pin1
  VCC: Adafruit_Qwiic_/_Stemma_QT_5_Port_Hub1.VCC, Adafrit_Precision_Volt_Ref.VIN, 5V.pin1, 5V.pin2, 5V.pin3, 5V.pin4, 5V.pin5, 5V.pin6, Arduino_Nano.5V
  N2: Adafruit_Qwiic_/_Stemma_QT_5_Port_Hub1.SDA, Arduino_Nano.A4
  N3: Adafruit_Qwiic_/_Stemma_QT_5_Port_Hub1.SCL, Arduino_Nano.A5
  N4: Adafrit_Precision_Volt_Ref.2.048V, 100_ohm.Pin_0
  N5: Arduino_Nano.D9, D9_/_A0.pin2
  N6: Arduino_Nano.A0, D9_/_A0.pin1

custom parts:
  Adafruit MCP3421 18-Bit ADC: The Adafruit MCP3421 18-Bit ADC is a simple, inexpensive, and easy to use 18-bit, 240 SPS, single-channel ADC with an I2C interface that can run up to 3.4MHz clock rate. A perfect component whenever you need an ADC that has differential inputs, adjustable gain, and a built in precision/low-drift reference voltage. One of the trade-offs with getting 18-bit precision is that the ADC is not going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
  Adafruit Qwiic / Stemma QT 5 Port Hub: Qwiic, or STEMMA QT, is a very efficient way to quickly prototype an idea, but a lot of Qwiic/Stemma QT driver boards only have one port, and devices have two ports but that's only good for chaining. Maybe you want to reduce your I2C line capacitance by having a star formation instead of a looooong chain. Or maybe its just easier for your mechanical layout to have them closer to a central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
  Adafruit LM4040 Voltage Reference: How good is your multimeter really? Or maybe your analog converter needs a good reference? Or lets say you want to test your microcontroller's conversion accuracy & precision. If only you had a dependable, high precision, rock-solid voltage reference. Now you know why we made this very cute and useful little breakout board. It has two very high precision shunt-type voltage references with 750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
